# Fritzing sketch new_complete_platform (saved by Fritzing 1.0.2b)
breadboards: 6

parts:
  CAN_LIN_Gateway = Arduino Mega 2560 (Rev3)
  CAN-Module = Niren can bus module [package=THT]
  S7 = Pushbutton [package="[THT]"]
  LED10 = RGB LED - (4 legs) [color="Red (633nm)" current=0.030A package="5 mm [THT]"]
  CAN_MULTI-MASTER_(RADAR) = Arduino Mega 2560 (Rev3)
  CAN-Module1 = Niren can bus module [package=THT]
  RADAR = US-100 Ultrasonic Distance Sensor
  LED11 = LED - 5mm [color="Red (633nm)" current=0.030A package="5 mm [THT]"]
  R-120ohm = Resistor [tolerance=±5% power=0.25W resistance=120 package=THT]
  R-120ohm1 = Resistor [tolerance=±5% power=0.25W resistance=120 package=THT]
  CAN_MULTI-MASTER_(DASH) = Arduino Mega 2560 (Rev3)
  CAN-Module2 = Niren can bus module [package=THT]
  LCD1 = LCD screen
  S8 = Pushbutton [package="[THT]"]
  MCP2003-MASTER = IC, DIP package, 8 pins [chip_label=MCP2003]
  R1_-_LIN_Pullup = Resistor [tolerance=±5% power=0.25W resistance=1k package=THT]
  S9 = Pushbutton [package="[THT]"]
  S10 = Pushbutton [package="[THT]"]
  LED12 = LED - 3mm [color="Green (555nm)" current=0.030A package="3 mm [THT]"]
  Diode = Diode [package=diode-1n4001]
  12V_PSU = BC9VPC [package=bc9vpc]
  LIN_Slave = Arduino Uno (Rev3) - ICSP
  MCP2003-SLAVE = IC, DIP package, 8 pins [chip_label=MCP2003]
  LED13 = LED - 3mm [color="Red (633nm)" current=0.030A package="3 mm [THT]"]
  LED14 = LED - 3mm [color="Yellow (595nm)" current=0.030A package="3 mm [THT]"]
  DHT = Humidity and Temperature Sensor DHT11

nets (from the schematic view):
  GND: CAN_LIN_Gateway.GND, CAN_LIN_Gateway.D8_PWM, CAN-Module.pin2, MCP2003-MASTER.pin5, S9.Pin_1, S9.Pin_2, LED12.cathode, 12V_PSU.V-, LIN_Slave.GND, MCP2003-SLAVE.pin5, LED13.cathode, LED14.cathode, DHT.GND_1
  N1: CAN_LIN_Gateway.D9_PWM, S10.Pin_1, S10.Pin_2
  N2: CAN_LIN_Gateway.5V, CAN-Module.pin1
  N3: CAN_LIN_Gateway.D0_RX0, MCP2003-MASTER.pin1
  N4: CAN_LIN_Gateway.D1_TX0, MCP2003-MASTER.pin4
  N5: CAN_LIN_Gateway.D2_PWM, CAN-Module.pin7
  N6: CAN_LIN_Gateway.D4_PWM, MCP2003-MASTER.pin2
  N7: CAN_LIN_Gateway.D40, S7.Pin_1, S7.Pin_2
  N8: CAN_LIN_Gateway.D42, LED10.red_cathode
  N9: CAN_LIN_Gateway.D43, LED10.green_cathode
  N10: CAN_LIN_Gateway.D44, LED10.blue_cathode
  N11: CAN_LIN_Gateway.D50, CAN-Module.pin4
  N12: CAN_LIN_Gateway.D51, CAN-Module.pin5
  N13: CAN_LIN_Gateway.D52, CAN-Module.pin6
  N14: CAN_LIN_Gateway.D53, CAN-Module.pin3
  N15: CAN-Module.pin8, R-120ohm.Pin_1
  N16: CAN-Module.pin9, R-120ohm.Pin_0
  N17: CAN-Module.pin10, CAN-Module.pin12
  N18: CAN-Module.pin11, CAN-Module.pin13, CAN-Module1.pin11, CAN-Module1.pin13, CAN-Module2.pin10, CAN-Module2.pin11, CAN-Module2.pin12, CAN-Module2.pin13
  N19: S7.Pin_3, S7.Pin_4, LED10.common_anode
  N20: CAN_MULTI-MASTER_(RADAR).GND, CAN-Module1.pin2
  N21: CAN_MULTI-MASTER_(RADAR).D9_PWM, RADAR.TRIG
  N22: CAN_MULTI-MASTER_(RADAR).D8_PWM, RADAR.ECHO
  5V: CAN_MULTI-MASTER_(RADAR).5V, CAN-Module1.pin1, RADAR.VCC
  N23: CAN_MULTI-MASTER_(RADAR).D2_PWM, CAN-Module1.pin7
  N24: CAN_MULTI-MASTER_(RADAR).D7_PWM, LED11.anode
  N25: CAN_MULTI-MASTER_(RADAR).D50, CAN-Module1.pin4
  N26: CAN_MULTI-MASTER_(RADAR).D51, CAN-Module1.pin5
  N27: CAN_MULTI-MASTER_(RADAR).D52, CAN-Module1.pin6
  N28: CAN_MULTI-MASTER_(RADAR).D53, CAN-Module1.pin3
  N29: RADAR.GND, RADAR.GND-2, LED11.cathode
  N30: R-120ohm1.Pin_0, CAN-Module2.pin9
  N31: R-120ohm1.Pin_1, CAN-Module2.pin8
  N32: CAN_MULTI-MASTER_(DASH).D13_PWM, LCD1.E
  N33: CAN_MULTI-MASTER_(DASH).D12_PWM, LCD1.RS
  N34: CAN_MULTI-MASTER_(DASH).D11_PWM, LCD1.DB4
  N35: CAN_MULTI-MASTER_(DASH).D10_PWM, LCD1.DB5
  N36: CAN_MULTI-MASTER_(DASH).D9_PWM, LCD1.DB6
  N37: CAN_MULTI-MASTER_(DASH).D8_PWM, LCD1.DB7
  N38: CAN_MULTI-MASTER_(DASH).D2_PWM, CAN-Module2.pin7
  5V_2: CAN_MULTI-MASTER_(DASH).5V, CAN-Module2.pin1, LCD1.VDD, LCD1.LED+
  GND_2: CAN_MULTI-MASTER_(DASH).D40, CAN_MULTI-MASTER_(DASH).GND, CAN-Module2.pin2, LCD1.VSS, LCD1.V0, LCD1.R/W, LCD1.LED-, S8.Pin_3, S8.Pin_4
  N39: CAN_MULTI-MASTER_(DASH).D50, CAN-Module2.pin4
  N40: CAN_MULTI-MASTER_(DASH).D51, CAN-Module2.pin5
  N41: CAN_MULTI-MASTER_(DASH).D52, CAN-Module2.pin6
  N42: CAN_MULTI-MASTER_(DASH).D53, CAN-Module2.pin3
  N43: S8.Pin_1, S8.Pin_2
  N44: MCP2003-MASTER.pin6, MCP2003-SLAVE.pin6
  N45: MCP2003-MASTER.pin7, R1_-_LIN_Pullup.Pin_0, Diode.C, MCP2003-SLAVE.pin7
  N46: S9.Pin_3, S9.Pin_4
  N47: S10.Pin_3, S10.Pin_4
  5V_3: LIN_Slave.5V, DHT.Vcc
  N48: LIN_Slave.D8, LED14.anode
  N49: LIN_Slave.D9_PWM, LED13.anode
  N50: LIN_Slave.D0/RX, MCP2003-SLAVE.pin1
  N51: LIN_Slave.D1/TX, MCP2003-SLAVE.pin4
  N52: LIN_Slave.D4, MCP2003-SLAVE.pin2
  N53: LIN_Slave.D5_PWM, DHT.Data-signal

custom parts:
  Niren can bus module: Niren can bus module availabe on ebay and others. Pcb view assumes that you unsolder the 7 pin header and resolder it on the bottom of the module to connect to the pcb. The two jumpers and the can bus connector remain on the top of the board and don't appear in pcb view.
  Humidity and Temperature Sensor DHT11: Digital relative humidity & temperature sensor DHT11
