# Fritzing sketch CAN_ONLY (saved by Fritzing 1.0.2b)
breadboards: 3

parts:
  CAN_LIN_Gateway = Arduino Mega 2560 (Rev3)
  CAN-Module = Niren can bus module [package=THT]
  S7 = Pushbutton [package="[THT]"]
  LED10 = RGB LED - (4 legs) [color="Red (633nm)" current=0.030A package="5 mm [THT]"]
  CAN_MULTI-MASTER_(RADAR) = Arduino Mega 2560 (Rev3)
  CAN-Module1 = Niren can bus module [package=THT]
  RADAR = US-100 Ultrasonic Distance Sensor
  LED11 = LED - 5mm [color="Red (633nm)" current=0.030A package="5 mm [THT]"]
  R-120ohm = Resistor [tolerance=±5% power=0.25W resistance=120 package=THT]
  R-120ohm1 = Resistor [tolerance=±5% power=0.25W resistance=120 package=THT]
  CAN_MULTI-MASTER_(DASH) = Arduino Mega 2560 (Rev3)
  CAN-Module2 = Niren can bus module [package=THT]
  LCD1 = LCD screen
  S8 = Pushbutton [package="[THT]"]

nets (from the schematic view):
  N1: CAN_LIN_Gateway.5V, CAN-Module.pin1
  N2: CAN_LIN_Gateway.GND, CAN-Module.pin2
  N3: CAN_LIN_Gateway.D2_PWM, CAN-Module.pin7
  N4: CAN_LIN_Gateway.D40, S7.Pin_1, S7.Pin_2
  N5: CAN_LIN_Gateway.D42, LED10.red_cathode
  N6: CAN_LIN_Gateway.D43, LED10.green_cathode
  N7: CAN_LIN_Gateway.D44, LED10.blue_cathode
  N8: CAN_LIN_Gateway.D50, CAN-Module.pin4
  N9: CAN_LIN_Gateway.D51, CAN-Module.pin5
  N10: CAN_LIN_Gateway.D52, CAN-Module.pin6
  N11: CAN_LIN_Gateway.D53, CAN-Module.pin3
  N12: CAN-Module.pin8, R-120ohm.Pin_1
  N13: CAN-Module.pin9, R-120ohm.Pin_0
  N14: CAN-Module.pin11, CAN-Module.pin13, CAN-Module1.pin11, CAN-Module1.pin13, CAN-Module2.pin10, CAN-Module2.pin11, CAN-Module2.pin12, CAN-Module2.pin13
  N15: S7.Pin_3, S7.Pin_4, LED10.common_anode
  N16: CAN_MULTI-MASTER_(RADAR).GND, CAN-Module1.pin2
  N17: CAN_MULTI-MASTER_(RADAR).D9_PWM, RADAR.TRIG
  N18: CAN_MULTI-MASTER_(RADAR).D8_PWM, RADAR.ECHO
  5V: CAN_MULTI-MASTER_(RADAR).5V, CAN-Module1.pin1, RADAR.VCC
  N19: CAN_MULTI-MASTER_(RADAR).D2_PWM, CAN-Module1.pin7
  N20: CAN_MULTI-MASTER_(RADAR).D7_PWM, LED11.anode
  N21: CAN_MULTI-MASTER_(RADAR).D50, CAN-Module1.pin4
  N22: CAN_MULTI-MASTER_(RADAR).D51, CAN-Module1.pin5
  N23: CAN_MULTI-MASTER_(RADAR).D52, CAN-Module1.pin6
  N24: CAN_MULTI-MASTER_(RADAR).D53, CAN-Module1.pin3
  N25: CAN-Module1.pin10, CAN-Module1.pin12
  N26: RADAR.GND, RADAR.GND-2, LED11.cathode
  N27: R-120ohm1.Pin_0, CAN-Module2.pin9
  N28: R-120ohm1.Pin_1, CAN-Module2.pin8
  N29: CAN_MULTI-MASTER_(DASH).D13_PWM, LCD1.E
  N30: CAN_MULTI-MASTER_(DASH).D12_PWM, LCD1.RS
  N31: CAN_MULTI-MASTER_(DASH).D11_PWM, LCD1.DB4
  N32: CAN_MULTI-MASTER_(DASH).D10_PWM, LCD1.DB5
  N33: CAN_MULTI-MASTER_(DASH).D9_PWM, LCD1.DB6
  N34: CAN_MULTI-MASTER_(DASH).D8_PWM, LCD1.DB7
  N35: CAN_MULTI-MASTER_(DASH).D2_PWM, CAN-Module2.pin7
  5V_2: CAN_MULTI-MASTER_(DASH).5V, CAN-Module2.pin1, LCD1.VDD, LCD1.LED+
  GND: CAN_MULTI-MASTER_(DASH).D40, CAN_MULTI-MASTER_(DASH).GND, CAN-Module2.pin2, LCD1.VSS, LCD1.V0, LCD1.R/W, LCD1.LED-, S8.Pin_3, S8.Pin_4
  N36: CAN_MULTI-MASTER_(DASH).D50, CAN-Module2.pin4
  N37: CAN_MULTI-MASTER_(DASH).D51, CAN-Module2.pin5
  N38: CAN_MULTI-MASTER_(DASH).D52, CAN-Module2.pin6
  N39: CAN_MULTI-MASTER_(DASH).D53, CAN-Module2.pin3
  N40: S8.Pin_1, S8.Pin_2

custom parts:
  Niren can bus module: Niren can bus module availabe on ebay and others. Pcb view assumes that you unsolder the 7 pin header and resolder it on the bottom of the module to connect to the pcb. The two jumpers and the can bus connector remain on the top of the board and don't appear in pcb view.
