# Fritzing sketch LIN_plat (saved by Fritzing 1.0.2b)
breadboards: 3

parts:
  MCP2003-SLAVE2 = IC, DIP package, 8 pins [chip_label=MCP2003]
  LED8 = LED - 3mm [color="Red (633nm)" current=0.030A package="3 mm [THT]"]
  LIN_Slave = Arduino Uno (Rev3) - ICSP
  LED7 = LED - 3mm [color="Yellow (595nm)" current=0.030A package="3 mm [THT]"]
  Diode2 = Diode [package=diode-1n4001]
  9V_Battery2 = BC9VPC [package=bc9vpc]
  DHT1 = Humidity and Temperature Sensor DHT11
  MCP2003-MASTER = IC, DIP package, 8 pins [chip_label=MCP2003]
  R1_-_LIN_Pullup3 = Resistor [tolerance=±5% power=0.25W resistance=1k package=THT]
  CAN_LIN_Gateway = Arduino Mega 2560 (Rev3)
  S5 = Pushbutton [package="[THT]"]
  S6 = Pushbutton [package="[THT]"]
  LED9 = LED - 3mm [color="Green (555nm)" current=0.030A package="3 mm [THT]"]

nets (from the schematic view):
  N1: MCP2003-SLAVE2.pin1, LIN_Slave.D0/RX
  N2: MCP2003-SLAVE2.pin2, LIN_Slave.D4
  N3: MCP2003-SLAVE2.pin4, LIN_Slave.D1/TX
  GND: MCP2003-SLAVE2.pin5, LIN_Slave.GND, MCP2003-MASTER.pin5, CAN_LIN_Gateway.GND
  N4: MCP2003-SLAVE2.pin7, Diode2.C
  N5: LED8.anode, LIN_Slave.D9_PWM
  N6: LIN_Slave.D8, LED7.anode
  N7: LIN_Slave.D5_PWM, DHT1.Data-signal
  5V: LIN_Slave.5V, DHT1.Vcc
  N8: Diode2.A, 9V_Battery2.V+
  N9: MCP2003-MASTER.pin1, CAN_LIN_Gateway.D0_RX0
  N10: MCP2003-MASTER.pin2, CAN_LIN_Gateway.D4_PWM
  N11: MCP2003-MASTER.pin4, CAN_LIN_Gateway.D1_TX0
  N12: MCP2003-MASTER.pin6, R1_-_LIN_Pullup3.Pin_1
  N13: MCP2003-MASTER.pin7, R1_-_LIN_Pullup3.Pin_0
  N14: CAN_LIN_Gateway.D10_PWM, LED9.anode
  N15: CAN_LIN_Gateway.D9_PWM, S6.Pin_1, S6.Pin_2
  N16: CAN_LIN_Gateway.D8_PWM, S5.Pin_1, S5.Pin_2
  N17: S5.Pin_3, S5.Pin_4
  N18: S6.Pin_3, S6.Pin_4, LED9.cathode

custom parts:
  Humidity and Temperature Sensor DHT11: Digital relative humidity & temperature sensor DHT11
